# Fritzing sketch esquematico (saved by Fritzing 0.9.6b)

parts:
  Componente2 = MPL3115A2 I2C Barometric Pressure, Altitude, Temperature Sensor
  Componente3 = Adafruit AHT20 Temperature and Humidity Sensor [part_number="Adafruit #4566"]
  Componente5 = GY-VL53L0XV2 Laser Ranger Module
  LCD1 = LCD screen
  R1 = Rotary Potentiometer (Large) [maximum_resistance=10kΩ package=THT]
  R2 = Resistor [tolerance=±5% resistance=330 package="2010 [SMD]"]
  Componente1 = Arduino Uno (Rev3)

nets:
  VCC: Componente2.VIN, Componente3.VCC, Componente5.VCC, LCD1.VDD, LCD1.LED+, R2.Pin_1, Componente1.5V
  GND: Componente2.GND, Componente3.GND, Componente5.GND, LCD1.VSS, LCD1.R/W, LCD1.LED-, R1.leg2, Componente1.GND
  N1: Componente2.SCL, Componente3.SCL, Componente5.SCL, Componente1.A5/SCL
  N2: Componente2.SDA, Componente3.SDA, Componente5.SDA, Componente1.A4/SDA
  N3: LCD1.V0, R1.wiper
  N4: LCD1.RS, Componente1.D12/MISO
  N5: LCD1.E, Componente1.D8
  N6: LCD1.DB4, Componente1.D5_PWM
  N7: LCD1.DB5, Componente1.D4
  N8: LCD1.DB6, Componente1.D3_PWM
  N9: LCD1.DB7, Componente1.D2
  N10: R1.leg1, R2.Pin_0

custom parts:
  MPL3115A2 I2C Barometric Pressure, Altitude, Temperature Sensor: This pressure sensor from Freescale is a great low-cost sensing solution for precision measurement of barometric pressure and altitude. The MPL3115A2 has a typical 1.5 Pascal resolution, which can resolve altitude at 0.3 meters (compare to the BMP180 which can do 0.17m). It has some upsides compared to the BMP180, such as interrupt outputs for ultra-low power usage, and its also a heck of a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
  Adafruit AHT20 Temperature and Humidity Sensor: The AHT20 is a nice but inexpensive temperature and humidity sensor from the same folks that brought us the DHT22. You can take sensor readings as often as you like, and it uses standard I2C so its super easy to use with any Arduino or Linux/Raspberry Pi board. This sensor has a typical accuracy of +- 2% relative humidity, and +-0.3 °C. There is only one I2C address so its not a good option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
  GY-VL53L0XV2 Laser Ranger Module: The GY-VL53L0XV2 is based on the VL53L0X from ST Microelectronics, a time-of-flight ranging system integrated into a compact module.
